// Logisim project cpu.circ as structural Verilog: 1 circuit, main circuit cpu
module cpu (
);

  wire ALU_Src, Reg_Dest, Reg_Write, undriven, Zero;
  wire [1:0] PC_control, Shift_Select;
  wire [4:0] ALU_Ctrl, multiplexer_2_out, multiplexer_5_out;
  wire [5:0] Func, opcode;
  wire [15:6] Imm;
  wire [25:16] J_ADD;
  wire [27:0] PC;
  wire [31:0] J_value, multiplexer_4_out, newPC, PC_4, PC_4_Imm, Read_Data1, Read_Data2, Result,
       shifter_1_out;
  wire [31:16] Imm_ext;

  Register #(.width(32)) u_PC (.D(newPC), .Q({J_value[31:28], PC}));  // open: en, clk, clr
  Shifter #(.width(32)) shifter_1 (.in({Imm_ext, Imm, Func}), .\dist (5'b00010), .out(shifter_1_out));
  Shifter #(.width(28)) shifter_2 (.in({2'b00, J_ADD, Imm, Func}), .\dist (5'b00010), .out(J_value[27:0]));
  Multiplexer #(.select(2), .width(32)) multiplexer_1 (
    .in0(PC_4), .in1(PC_4_Imm), .in2(J_value), .in3(Read_Data1), .out(newPC), .sel(PC_control));
  Adder #(.width(32)) adder_1 (.a({J_value[31:28], PC}), .b(32'h4), .out(PC_4));  // open: cin, cout
  Adder #(.width(32)) adder_2 (.a(PC_4), .b(shifter_1_out), .out(PC_4_Imm));  // open: cin, cout
  mem InstMem (
    .MemAddress({J_value[31:28], PC}), .clk(undriven), .MemReadData({opcode, J_ADD, Imm, Func}));  // open: MemWriteMask, MemWriteData
  Multiplexer #(.width(5)) multiplexer_2 (
    .in0(J_ADD[20:16]), .in1(Imm[15:11]), .out(multiplexer_2_out), .sel(Reg_Dest));
  Multiplexer #(.width(16)) multiplexer_3 (.in0({16{1'b0}}), .in1({16{1'b1}}), .out(Imm_ext), .sel(Imm[15]));
  control_unit CU (
    .Reg_Dest(Reg_Dest), .ALU_Src(ALU_Src), .Reg_Write(Reg_Write));  // open: opcode, Jump, Branch, Mem_Read, Mem_to_Reg, Mem_Write
  // regfile RegisterFile: pin names not known; wires that end beside it: J_ADD[25:21], J_ADD[20:16], multiplexer_2_out, Reg_Write, Read_Data1, Read_Data2
  Multiplexer #(.width(32)) multiplexer_4 (
    .in0(Read_Data2), .in1({Imm_ext, Imm, Func}), .out(multiplexer_4_out), .sel(ALU_Src));
  Multiplexer #(.select(2), .width(5)) multiplexer_5 (
    .in0(Imm[10:6]), .in1(Read_Data1[4:0]), .in2(5'b10000), .in3({5{1'b0}}), .out(multiplexer_5_out),
    .sel(Shift_Select));
  // alu_control_unit ALU_Control: pin names not known; wires that end beside it: Func, opcode, ALU_Ctrl, Shift_Select
  ALU ArithLogicUnit (
    .Input1(Read_Data1), .Input2(multiplexer_4_out), .op(ALU_Ctrl), .SHA(multiplexer_5_out), .Zero(Zero),
    .Result(Result));
  // mem DataMem: pin names not known

  // Other names for the same wires on the sheet: rt[4:0] = J_ADD[20:16]; rs[4:0] = J_ADD[25:21]; Imm[5:0] = Func;
  //   Imm_ext[15:0] = {Imm, Func}; J_ADD[15:0] = {Imm, Func}; SHA[4:0] = Imm[10:6]; rd[4:0] = Imm[15:11];
  //   PC[31:28] = J_value[31:28]

  // Notes on the sheet:
  //   Branch
  //   JR
  //   PC Logic
  //   Next
  //   Jump
  //   Sign Extend
endmodule
